# Fritzing sketch Tallbike (saved by Fritzing 0.9.2b)

parts:
  Bauteil1 = Arduino Uno (Rev3)
  Schrittmotor = Stepper Motor - Bipolar
  V1 = DC Power [voltage=12V]
  V2 = DC Power [voltage=5]
  Relay = Relay [part_number=FRS1B-S package=THT]
  Motorshield = Dual VNH2SP30 Motor Driver [part_number=MD03A]
  230V_Spannungswandler = Screw terminal - 2 pins [package=THT]
  MP3_GND_VCC_Li_Re_____B1_B2_B3_B4 = female pin header, 10 pins [form="♀ (female)"]
  MP3_GND_VCC_Li_Re_____B1_B2_B3_B5 = female pin header, 10 pins [form="♀ (female)"]
  Audiobuchse = Audio Jack (TRRS) 3.5mm [part_number="LUMBERG JEITA RC-5325A" package="RC-5325A [SMD]"]
  Stimmung = Pushbutton [package="[THT]"]
  Effekt = Pushbutton [package="[THT]"]

nets:
  N1: Bauteil1.A0, MP3_GND_VCC_Li_Re_____B1_B2_B3_B5.pin4
  N2: Bauteil1.A1, MP3_GND_VCC_Li_Re_____B1_B2_B3_B5.pin3
  N3: Bauteil1.A2, MP3_GND_VCC_Li_Re_____B1_B2_B3_B5.pin2
  N4: Bauteil1.A3, MP3_GND_VCC_Li_Re_____B1_B2_B3_B5.pin1
  N5: Bauteil1.A4/SDA, Stimmung.Pin_4
  N6: Bauteil1.A5/SCL, Effekt.Pin_4
  N7: Bauteil1.D8, Motorshield.1INa
  N8: Bauteil1.D9_PWM, Motorshield.1INb
  N9: Bauteil1.D11_PWM/MOSI, Motorshield.2INb#142
  N10: Bauteil1.D12/MISO, Motorshield.2INb#143
  N11: Bauteil1.D3_PWM, MP3_GND_VCC_Li_Re_____B1_B2_B3_B4.pin1
  N12: Bauteil1.D4, MP3_GND_VCC_Li_Re_____B1_B2_B3_B4.pin2
  N13: Bauteil1.D5_PWM, MP3_GND_VCC_Li_Re_____B1_B2_B3_B4.pin3
  N14: Bauteil1.D6_PWM, MP3_GND_VCC_Li_Re_____B1_B2_B3_B4.pin4
  N15: Bauteil1.D7, Relay.COIL1
  N16: Bauteil1.5V, V2.V+, Motorshield.+5V_(IN), MP3_GND_VCC_Li_Re_____B1_B2_B3_B4.pin9, MP3_GND_VCC_Li_Re_____B1_B2_B3_B5.pin9
  N17: Bauteil1.GND, MP3_GND_VCC_Li_Re_____B1_B2_B3_B4.pin10, MP3_GND_VCC_Li_Re_____B1_B2_B3_B5.pin10, Audiobuchse.TIP, Stimmung.Pin_1, Stimmung.Pin_2, Effekt.Pin_1, Effekt.Pin_2
  N18: Schrittmotor.A, Motorshield.OUT_1A
  N19: Schrittmotor.C, Motorshield.OUT_1B
  N20: Schrittmotor.B, Motorshield.OUT_2A
  N21: Schrittmotor.D, Motorshield.OUT_2B
  N22: V1.V+, Relay.C1, Relay.C2, Motorshield.VIN
  N23: V1.V-, V2.V-, Relay.COIL2, Motorshield.GND, 230V_Spannungswandler.pin1
  N24: Relay.A, 230V_Spannungswandler.pin2
  N25: MP3_GND_VCC_Li_Re_____B1_B2_B3_B4.pin7, MP3_GND_VCC_Li_Re_____B1_B2_B3_B5.pin7, Audiobuchse.RING2
  N26: MP3_GND_VCC_Li_Re_____B1_B2_B3_B4.pin8, MP3_GND_VCC_Li_Re_____B1_B2_B3_B5.pin8, Audiobuchse.RING1

notes:
  Tallbike, Arduino mit Motorshield, Relay und zwei MP3-Spielern
